# Fritzing sketch n2k_dashboard (saved by Fritzing 1.0.6)

parts:
  Buck_Converter = RioRand LM2596
  Part3 = Adafruit ESP32-S3 Reverse TFT Feather [part_number="Adafruit #5691"]
  F1_0_2A1 = FUSE [package=fuse_5mm]
  Adafruit_CAN_Pal_Breakout1 = Adafruit CAN Pal Breakout [part_number=#5708]
  Adafruit_BMP580_Temperature_and_Pressure_Sensor_(optional) = Adafruit BMP581 Temperature and Pressure Sensor [part_number=#6407]  # not connected

nets:
  N1: Buck_Converter.Pin_1, F1_0_2A1.2
  N2K CAN GND: Buck_Converter.Pin_2
  N2: Buck_Converter.Pin_3, Part3.VBUS
  GND: Buck_Converter.Pin_4, Part3.GND, Adafruit_CAN_Pal_Breakout1.GND
  3.3V: Part3.3.3V, Adafruit_CAN_Pal_Breakout1.VCC
  N3: Part3.D9, Adafruit_CAN_Pal_Breakout1.CAN1_S
  N4: Part3.D6, Adafruit_CAN_Pal_Breakout1.CAN1_TX
  N5: Part3.D5, Adafruit_CAN_Pal_Breakout1.CAN1_RX
  N2K CAN-H: Adafruit_CAN_Pal_Breakout1.CAN_H
  N2K CAN-L: Adafruit_CAN_Pal_Breakout1.CAN_L

notes:
  N2K 12V
  N2K GND
  N2K CAN-H
  N2K CAN-L
  USB GND
  USB VBUS
  5V
  Connected via STEMMA QT

custom parts:
  Adafruit CAN Pal Breakout: If you'd like to connect a board with native CAN Peripheral support, the Adafruit CAN Pal Transceiver will take the 3V logic level signals and convert them to CAN logic levels with the differential signaling required to communicate. Note that not all chips have a CAN peripheral! Some that we know do have it are the ESP32/ESP32-S2/ESP32-S3 (note that ESP32 calls this interface TWAI not CAN)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
  Adafruit BMP581 Temperature and Pressure Sensor: Bosch has been a leader in barometric pressure sensors, from the BMP085. BMP180, BMP280, BMP388, BMP390... now we've got the next generation, the Adafruit BMP58x Precision Barometric Pressure and Altimeter Breakout. As you would expect, this sensor is similar to its earlier versions but even better. The BMP581 has better precision than ever, which makes it excellent for environmental sensing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
